# Fritzing sketch arduino-pot-servo (saved by Fritzing 0.9.0b)
breadboards: 1

parts:
  Part1 = Arduino Uno (Rev3)
  U1 = POT [package=pot_mammoth]
  LED1 = LED - 5mm [color="Red (633nm)" package="5 mm [THT]"]
  J1 = Basic Servo

nets:
  N1: Part1.D9_PWM, U1.A
  N2: Part1.D13/SCK, LED1.anode
  GND: Part1.GND, U1.S, LED1.cathode, J1.gnd
  N3: Part1.D2, J1.pulse
  5V: Part1.5V, U1.E, J1.vcc
